// Logisim project cpu.circ as structural Verilog: 1 circuit, main circuit main
module main (
);

  wire and_1_out, button_1_out, clock_1_out, demultiplexer_1_out0, demultiplexer_1_out1,
       demultiplexer_1_out2, demultiplexer_1_out3, multiplexer_2_out, not_1_out, not_2_out, xor_1_out;
  wire [1:0] multiplexer_1_out, multiplexer_3_out, multiplexer_9_out;
  wire [3:0] multiplexer_4_out, multiplexer_5_out, multiplexer_6_out, multiplexer_6_out_2, multiplexer_7_out;
  wire [6:0] multiplexer_10_out;
  wire [7:0] adder_1_out, multiplexer_8_out, register_1_q, register_2_q, register_3_q, register_4_q,
       register_5_q, rom_1_data;
  wire [7:7] multiplexer_10_out_2;

  ROM rom_1 (.addr(register_1_q), .data(rom_1_data));
  Clock clock_1 (.out(clock_1_out));
  LED led_1 (.in(clock_1_out));
  Register register_1 (.D(adder_1_out), .en(1'b1), .clk(clock_1_out), .Q(register_1_q), .clr(button_1_out));
  Button button_1 (.out(button_1_out));
  // Probe on rom_1_data
  Adder adder_1 (.a(register_1_q), .b(8'h1), .out(adder_1_out), .cin(1'b0));  // open: cout
  Multiplexer #(.width(2), .enable("false")) multiplexer_1 (
    .in0(2'b00), .in1(rom_1_data[5:4]), .out(multiplexer_1_out), .sel(not_1_out));
  not not_1 (not_1_out, rom_1_data[7]);
  Register register_2 (
    .D(multiplexer_8_out), .en(demultiplexer_1_out0), .clk(clock_1_out), .Q(register_2_q), .clr(button_1_out));
  Demultiplexer #(.select(2), .enable("false")) demultiplexer_1 (
    .out0(demultiplexer_1_out0), .out1(demultiplexer_1_out1), .out2(demultiplexer_1_out2),
    .out3(demultiplexer_1_out3), .in(multiplexer_2_out), .sel(multiplexer_1_out));
  // Probe on multiplexer_2_out
  Multiplexer #(.enable("false")) multiplexer_2 (.in0(not_1_out), .in1(xor_1_out), .out(multiplexer_2_out), .sel(1'b0));
  Multiplexer #(.width(2), .enable("false")) multiplexer_3 (
    .in0(2'b00), .in1(rom_1_data[5:4]), .out(multiplexer_3_out), .sel(not_1_out));
  Multiplexer #(.width(4), .enable("false")) multiplexer_4 (
    .in0(multiplexer_6_out_2), .in1(multiplexer_6_out), .out(multiplexer_4_out), .sel(rom_1_data[6]));
  Register register_3 (
    .D(multiplexer_8_out), .en(demultiplexer_1_out1), .clk(clock_1_out), .Q(register_3_q), .clr(button_1_out));
  Multiplexer #(.width(4), .enable("false")) multiplexer_5 (
    .in0(rom_1_data[3:0]), .in1(multiplexer_4_out), .out(multiplexer_5_out), .sel(rom_1_data[6]));
  Register register_4 (
    .D(multiplexer_8_out), .en(demultiplexer_1_out2), .clk(clock_1_out), .Q(register_4_q), .clr(button_1_out));
  Multiplexer #(.select(2), .width(8), .enable("false")) multiplexer_6 (
    .in0(register_2_q), .in1(register_3_q), .in2(register_4_q), .in3(register_5_q),
    .out({multiplexer_6_out_2, multiplexer_6_out}), .sel(multiplexer_3_out));
  // Probe on {multiplexer_6_out_2, multiplexer_6_out}
  Multiplexer #(.width(4), .enable("false")) multiplexer_7 (
    .in0(multiplexer_4_out), .in1(rom_1_data[3:0]), .out(multiplexer_7_out), .sel(rom_1_data[6]));
  // Probe on multiplexer_8_out
  Multiplexer #(.width(8), .enable("false")) multiplexer_8 (
    .in0({8{1'b0}}), .in1({multiplexer_7_out, multiplexer_5_out}), .out(multiplexer_8_out), .sel(not_1_out));
  Register register_5 (
    .D(multiplexer_8_out), .en(demultiplexer_1_out3), .clk(clock_1_out), .Q(register_5_q), .clr(button_1_out));
  Multiplexer #(.width(2), .enable("false")) multiplexer_9 (
    .in0(2'b00), .out(multiplexer_9_out), .sel(1'b0));  // open: in1
  TTY tty_1 (.data(multiplexer_10_out), .clk(clock_1_out), .we(and_1_out), .clr(multiplexer_10_out_2[7]));
  xor xor_1 (xor_1_out, rom_1_data[5], rom_1_data[6]);
  Multiplexer #(.select(2), .width(8), .enable("false")) multiplexer_10 (
    .in0(register_2_q), .in1(register_3_q), .in2(register_4_q), .in3(multiplexer_8_out),
    .out({multiplexer_10_out_2[7], multiplexer_10_out}), .sel(multiplexer_9_out));
  // Probe on {multiplexer_10_out_2[7], multiplexer_10_out}
  and and_1 (and_1_out, rom_1_data[7], not_2_out);
  not not_2 (not_2_out, xor_1_out);

  // Notes on the sheet:
  //   contents of rom_1 (hex, n*v repeats v):
  //   e 46 f0 f 46 f0 b 46 f0 5 47 f0 4 46 f0 f 46 f0 0 42 f0 3 46 f0 5 47 f0 2 47 f0 9 46 f0 f 46 f0 3 47
  //   f0 f 46 f0 a 40 f0
  //   RESET
  //   PC
  //   WRITE SELECT
  //   R0
  //   R1
  //   REG OUT A
  //   HI
  //   LO
  //   R2
  //   HI
  //   REG IN
  //   LO
  //   R3
  //   REG OUT B
endmodule
